# Fritzing sketch project_layout (saved by Fritzing 1.0.5)

parts:
  M1 = 1 chan 5v relay module
  Mod1 = Raspberry Pi Pico W
  R1 = Resistor [tolerance=±5% power=0.25W resistance=150 package=THT]
  LED1 = LED - 5mm [color="Red (633nm)" current=0.030A package="5 mm [THT]"]
  LED2 = LED - 5mm [color="Red (633nm)" current=0.030A package="5 mm [THT]"]
  R2 = Resistor [tolerance=±5% power=0.25W resistance=150 package=THT]
  VALVE1 = Plastic Solenoid Valve

nets:
  N1: M1.pin_1, Mod1.pin_36
  N2: M1.pin_2, Mod1.pin_3, Mod1.pin_23, Mod1.pin_28, Mod1.pin_38, Mod1.pin_42, LED1.anode, LED2.anode
  N3: M1.pin_3, Mod1.pin_34
  N4: M1.pin_4, VALVE1.no_name_yet#2
  N5: Mod1.pin_21, R1.Pin_0
  N6: Mod1.pin_27, R2.Pin_0
  N7: R1.Pin_1, LED1.cathode
  N8: LED2.cathode, R2.Pin_1

custom parts:
  1 chan 5v relay module: 1 Channel 5V Relay Module Board Shield with Optocoupler Support High and Low Level Trigger for Arduino.
  Raspberry Pi Pico W: Raspberry Pi Pico W. Based around the RP2040 microcontroller the Pico W is a low cost microcontroller device bringing Raspberry Pi quality, cost, and easy of use to the microcontroller space. The areas marked KEEPOUT in pcb silkscreen should not have traces running through them to avoid shorts on a soldered in module!
