# Fritzing sketch esp8266_BMP280_i2c (saved by Fritzing 1.0.5)

parts:
  Mod2 = Amica NodeMCU DEVKIT 1.0
  M1 = BME280

nets:
  N1: Mod2.pin_9, Mod2.pin_25, M1.GND
  N2: Mod2.pin_10, Mod2.pin_26, M1.VIN
  N3: Mod2.pin_13, M1.SDA
  N4: Mod2.pin_14, M1.SCL

custom parts:
  BME280: Temperature Humidity Barometric presure Sensor
